// Logisim project EstudioDeSumadores.circ as structural Verilog: 6 circuits, main circuit full_adder
module full_adder (
  input  X,
  input  Y,
  input  Ci,
  output Sum,
  output Co
);

  wire and_1_out, and_2_out, xor_1_out;

  xor xor_1 (xor_1_out, X, Y);
  xor xor_2 (Sum, xor_1_out, Ci);
  and and_1 (and_1_out, X, Y);
  and and_2 (and_2_out, Ci, xor_1_out);
  or or_1 (Co, and_1_out, and_2_out);
endmodule

module ripple_carry_adder (
  input  in_1,
  input  in_2,
  input  in_3,
  input  in_4,
  input  in_5,
  input  in_6,
  input  in_7,
  input  in_8,
  output out_9,
  output out_10,
  output out_11,
  output out_12,
  output out_13
);

  wire full_adder_1_co, full_adder_2_co, full_adder_3_co;

  LED led_1 (.in(out_9));
  full_adder full_adder_1 (.X(in_1), .Y(in_2), .Ci(1'b0), .Sum(out_9), .Co(full_adder_1_co));
  LED led_2 (.in(out_10));
  full_adder full_adder_2 (.X(in_3), .Y(in_4), .Ci(full_adder_1_co), .Sum(out_10), .Co(full_adder_2_co));
  LED led_3 (.in(out_11));
  full_adder full_adder_3 (.X(in_5), .Y(in_6), .Ci(full_adder_2_co), .Sum(out_11), .Co(full_adder_3_co));
  LED led_4 (.in(out_12));
  full_adder full_adder_4 (.X(in_7), .Y(in_8), .Ci(full_adder_3_co), .Sum(out_12), .Co(out_13));
  LED led_5 (.in(out_13));
endmodule

module half_adder (
  input  Y,
  input  X,
  output Sum,
  output Co
);

  xor xor_1 (Co, Y, X);
  and and_1 (Sum, Y, X);
endmodule

module prefix_adder (
  input  in_1,
  input  in_2,
  input  in_3,
  input  in_4,
  input  in_5,
  input  in_6,
  input  in_7,
  input  in_8,
  input  in_9,
  output out_10,
  output out_11,
  output out_12,
  output out_13,
  output out_14
);

  prefix prefix_1 (
    .X3(in_1), .X2(in_2), .X1(in_3), .X0(in_4), .Y3(in_5), .Y2(in_6), .Y1(in_7), .Y0(in_8), .Ci(in_9),
    .S3(out_10), .S2(out_11), .S1(out_12), .S0(out_13), .Co(out_14));
  LED led_1 (.in(out_10));
  LED led_2 (.in(out_11));
  LED led_3 (.in(out_12));
  LED led_4 (.in(out_13));
  LED led_5 (.in(out_14));
endmodule

module carry_lookahead_adder (
  input  Y,
  input  X,
  input  in_3,
  input  in_4,
  input  in_5,
  input  in_6,
  input  Ci,
  output out_8,
  output out_9,
  output out_10
);

  wire and_1_out, and_2_out, and_3_out, and_4_out, and_5_out, and_6_out, half_adder_1_co, half_adder_1_sum,
       half_adder_2_co, half_adder_2_sum, half_adder_3_co, half_adder_3_sum;

  half_adder half_adder_1 (.Y(Y), .X(X), .Sum(half_adder_1_sum), .Co(half_adder_1_co));
  half_adder half_adder_2 (.Y(in_3), .X(in_4), .Sum(half_adder_2_sum), .Co(half_adder_2_co));
  half_adder half_adder_3 (.Y(in_5), .X(in_6), .Sum(half_adder_3_sum), .Co(half_adder_3_co));
  and and_1 (and_1_out, Ci, half_adder_3_co, half_adder_2_co, half_adder_1_co);
  and and_2 (and_2_out, half_adder_3_sum, half_adder_2_co, half_adder_1_co);
  and and_3 (and_3_out, half_adder_1_co, half_adder_2_sum);
  and and_4 (and_4_out, Ci, half_adder_3_co, half_adder_2_co);
  and and_5 (and_5_out, half_adder_2_co, half_adder_3_sum);
  and and_6 (and_6_out, half_adder_3_co, Ci);
  LED led_1 (.in(out_8));
  or or_1 (out_8, and_1_out, and_2_out, and_3_out, half_adder_1_sum);
  LED led_2 (.in(out_9));
  or or_2 (out_9, and_4_out, half_adder_2_sum, and_5_out);
  LED led_3 (.in(out_10));
  or or_3 (out_10, half_adder_3_sum, and_6_out);
endmodule

module prefix (
  input  X3,
  input  X2,
  input  X1,
  input  X0,
  input  Y3,
  input  Y2,
  input  Y1,
  input  Y0,
  input  Ci,
  output S3,
  output S2,
  output S1,
  output S0,
  output Co
);

  wire not_1_out, not_2_out, not_3_out, not_4_out, not_5_out, not_6_out, not_7_out, not_8_out, not_9_out,
       or_1_out, or_2_out, or_3_out, or_4_out, or_5_out, or_6_out, or_7_out, or_8_out, or_9_out, or_10_out,
       or_11_out, or_12_out, or_13_out, or_14_out, or_15_out, or_16_out, or_17_out, or_18_out, or_19_out,
       or_20_out, or_21_out, or_22_out, or_23_out, or_24_out, or_25_out, or_26_out, or_27_out, or_28_out,
       or_29_out, or_30_out, or_31_out, or_32_out, or_33_out, or_34_out, or_35_out, or_36_out, or_37_out,
       or_38_out, or_39_out, or_40_out, or_41_out, or_42_out, or_43_out, or_44_out, or_45_out, or_46_out,
       or_47_out, or_48_out, or_49_out, or_50_out, or_51_out, or_52_out, or_53_out, or_54_out, or_55_out,
       or_56_out, or_57_out, or_58_out, or_59_out, or_60_out, or_61_out, or_62_out, or_63_out, or_64_out,
       or_65_out, or_66_out, or_67_out, or_68_out, or_69_out, or_70_out, or_71_out, or_72_out, or_73_out,
       or_74_out, or_75_out, or_76_out, or_77_out, or_78_out, or_79_out, or_80_out, or_81_out, or_82_out,
       or_83_out, or_84_out, or_85_out, or_86_out, or_87_out, or_88_out, or_89_out, or_90_out, or_91_out,
       or_92_out, or_93_out, or_94_out, or_95_out, or_96_out, or_97_out, or_98_out, or_99_out, or_100_out,
       or_101_out, or_102_out, or_103_out, or_104_out, or_105_out, or_106_out, or_107_out, or_108_out,
       or_109_out, or_110_out, or_111_out, or_112_out, or_113_out, or_114_out, or_115_out, or_116_out,
       or_117_out, or_118_out, or_119_out, or_120_out, or_121_out, or_122_out, or_123_out, or_124_out,
       or_125_out, or_126_out, or_127_out, or_128_out, or_129_out, or_130_out, or_131_out, or_132_out,
       or_133_out, or_134_out, or_135_out;

  not not_1 (not_1_out, X3);
  not not_2 (not_2_out, X2);
  not not_3 (not_3_out, X1);
  not not_4 (not_4_out, X0);
  not not_5 (not_5_out, Y3);
  not not_6 (not_6_out, Y2);
  not not_7 (not_7_out, Y1);
  not not_8 (not_8_out, Y0);
  not not_9 (not_9_out, Ci);
  or or_1 (or_1_out, X3, X2, Y3, Y2);
  or or_2 (or_2_out, X3, X2, X1, Y3, Y1);
  or or_3 (or_3_out, X3, X2, X1, X0, Y3, Y0);
  or or_4 (or_4_out, X3, X2, X1, X0, Y3, Ci);
  or or_5 (or_5_out, X3, not_5_out, not_6_out, not_7_out, not_8_out, not_9_out);
  or or_6 (or_6_out, X3, X2, X1, Y3, Y0, Ci);
  or or_7 (or_7_out, X3, not_4_out, not_5_out, not_6_out, not_7_out, not_9_out);
  or or_8 (or_8_out, X3, not_4_out, not_5_out, not_6_out, not_7_out, not_8_out);
  or or_9 (or_9_out, X3, X2, X0, Y3, Y1, Y0);
  or or_10 (or_10_out, X3, X2, X0, Y3, Y1, Ci);
  or or_11 (or_11_out, X3, not_3_out, not_5_out, not_6_out, not_8_out, not_9_out);
  or or_12 (or_12_out, X3, not_3_out, not_5_out, not_6_out, not_7_out);
  or or_13 (or_13_out, X3, X2, Y3, Y1, Y0, Ci);
  or or_14 (or_14_out, X3, not_3_out, not_4_out, not_5_out, not_6_out, not_9_out);
  or or_15 (or_15_out, X3, not_3_out, not_4_out, not_5_out, not_6_out, not_8_out);
  or or_16 (or_16_out, X3, X1, Y3, Y2, Y1);
  or or_17 (or_17_out, X3, X1, X0, Y3, Y2, Y0);
  or or_18 (or_18_out, X3, X1, X0, Y3, Y2, Ci);
  or or_19 (or_19_out, X3, not_2_out, not_5_out, not_7_out, not_8_out, not_9_out);
  or or_20 (or_20_out, X3, not_2_out, not_5_out, not_6_out);
  or or_21 (or_21_out, X3, X1, Y3, Y2, Y0, Ci);
  or or_22 (or_22_out, X3, not_2_out, not_4_out, not_5_out, not_7_out, not_9_out);
  or or_23 (or_23_out, X3, not_2_out, not_4_out, not_5_out, not_7_out, not_8_out);
  or or_24 (or_24_out, X3, X0, Y3, Y2, Y1, Y0);
  or or_25 (or_25_out, X3, X0, Y3, Y2, Y1, Ci);
  or or_26 (or_26_out, X3, not_2_out, not_3_out, not_5_out, not_8_out, not_9_out);
  or or_27 (or_27_out, X3, not_2_out, not_3_out, not_5_out, not_7_out);
  or or_28 (or_28_out, X3, Y3, Y2, Y1, Y0, Ci);
  or or_29 (or_29_out, X3, not_2_out, not_3_out, not_4_out, not_5_out, not_9_out);
  or or_30 (or_30_out, X3, not_2_out, not_3_out, not_4_out, not_5_out, not_8_out);
  or or_31 (or_31_out, not_1_out, Y3, not_6_out, not_7_out, not_8_out, not_9_out);
  or or_32 (or_32_out, not_1_out, X2, not_5_out, Y2);
  or or_33 (or_33_out, not_1_out, X2, X1, not_5_out, Y1);
  or or_34 (or_34_out, not_1_out, X2, X1, X0, not_5_out, Y0);
  or or_35 (or_35_out, not_1_out, X2, X1, X0, not_5_out, Ci);
  or or_36 (or_36_out, not_1_out, not_4_out, Y3, not_6_out, not_7_out, not_9_out);
  or or_37 (or_37_out, not_1_out, not_4_out, Y3, not_6_out, not_7_out, not_8_out);
  or or_38 (or_38_out, not_1_out, X2, X1, not_5_out, Y0, Ci);
  or or_39 (or_39_out, not_1_out, not_3_out, Y3, not_6_out, not_8_out, not_9_out);
  or or_40 (or_40_out, not_1_out, not_3_out, Y3, not_6_out, not_7_out);
  or or_41 (or_41_out, not_1_out, X2, X0, not_5_out, Y1, Y0);
  or or_42 (or_42_out, not_1_out, X2, X0, not_5_out, Y1, Ci);
  or or_43 (or_43_out, not_1_out, not_3_out, not_4_out, Y3, not_6_out, not_9_out);
  or or_44 (or_44_out, not_1_out, not_3_out, not_4_out, Y3, not_6_out, not_8_out);
  or or_45 (or_45_out, not_1_out, X2, not_5_out, Y1, Y0, Ci);
  or or_46 (or_46_out, not_1_out, not_2_out, Y3, not_7_out, not_8_out, not_9_out);
  or or_47 (or_47_out, not_1_out, not_2_out, Y3, not_6_out);
  or or_48 (or_48_out, not_1_out, X1, not_5_out, Y2, Y1);
  or or_49 (or_49_out, not_1_out, X1, X0, not_5_out, Y2, Y0);
  or or_50 (or_50_out, not_1_out, X1, X0, not_5_out, Y2, Ci);
  or or_51 (or_51_out, not_1_out, not_2_out, not_4_out, Y3, not_7_out, not_9_out);
  or or_52 (or_52_out, not_1_out, not_2_out, not_4_out, Y3, not_7_out, not_8_out);
  or or_53 (or_53_out, not_1_out, X1, not_5_out, Y2, Y0, Ci);
  or or_54 (or_54_out, not_1_out, not_2_out, not_3_out, Y3, not_8_out, not_9_out);
  or or_55 (or_55_out, not_1_out, not_2_out, not_3_out, Y3, not_7_out);
  or or_56 (or_56_out, not_1_out, X0, not_5_out, Y2, Y1, Y0);
  or or_57 (or_57_out, not_1_out, X0, not_5_out, Y2, Y1, Ci);
  or or_58 (or_58_out, not_1_out, not_2_out, not_3_out, not_4_out, Y3, not_9_out);
  or or_59 (or_59_out, not_1_out, not_2_out, not_3_out, not_4_out, Y3, not_8_out);
  or or_60 (or_60_out, not_1_out, not_5_out, Y2, Y1, Y0, Ci);
  or or_61 (or_61_out, X2, X1, Y2, Y1);
  or or_62 (or_62_out, X2, X1, X0, Y2, Y0);
  or or_63 (or_63_out, X2, X1, X0, Y2, Ci);
  or or_64 (or_64_out, X2, not_6_out, not_7_out, not_8_out, not_9_out);
  or or_65 (or_65_out, X2, X1, Y2, Y0, Ci);
  or or_66 (or_66_out, X2, not_4_out, not_6_out, not_7_out, not_9_out);
  or or_67 (or_67_out, X2, not_4_out, not_6_out, not_7_out, not_8_out);
  or or_68 (or_68_out, X2, X0, Y2, Y1, Y0);
  or or_69 (or_69_out, X2, X0, Y2, Y1, Ci);
  or or_70 (or_70_out, X2, not_3_out, not_6_out, not_8_out, not_9_out);
  or or_71 (or_71_out, X2, not_3_out, not_6_out, not_7_out);
  or or_72 (or_72_out, X2, Y2, Y1, Y0, Ci);
  or or_73 (or_73_out, X2, not_3_out, not_4_out, not_6_out, not_9_out);
  or or_74 (or_74_out, X2, not_3_out, not_4_out, not_6_out, not_8_out);
  or or_75 (or_75_out, not_2_out, Y2, not_7_out, not_8_out, not_9_out);
  or or_76 (or_76_out, not_2_out, X1, not_6_out, Y1);
  or or_77 (or_77_out, not_2_out, X1, X0, not_6_out, Y0);
  or or_78 (or_78_out, not_2_out, X1, X0, not_6_out, Ci);
  or or_79 (or_79_out, not_2_out, not_4_out, Y2, not_7_out, not_9_out);
  or or_80 (or_80_out, not_2_out, not_4_out, Y2, not_7_out, not_8_out);
  or or_81 (or_81_out, not_2_out, X1, not_6_out, Y0, Ci);
  or or_82 (or_82_out, not_2_out, not_3_out, Y2, not_8_out, not_9_out);
  or or_83 (or_83_out, not_2_out, not_3_out, Y2, not_7_out);
  or or_84 (or_84_out, not_2_out, X0, not_6_out, Y1, Y0);
  or or_85 (or_85_out, not_2_out, X0, not_6_out, Y1, Ci);
  or or_86 (or_86_out, not_2_out, not_3_out, not_4_out, Y2, not_9_out);
  or or_87 (or_87_out, not_2_out, not_3_out, not_4_out, Y2, not_8_out);
  or or_88 (or_88_out, not_2_out, not_6_out, Y1, Y0, Ci);
  or or_89 (or_89_out, X1, X0, Y1, Y0);
  or or_90 (or_90_out, X1, X0, Y1, Ci);
  or or_91 (or_91_out, X1, not_7_out, not_8_out, not_9_out);
  or or_92 (or_92_out, X1, Y1, Y0, Ci);
  or or_93 (or_93_out, X1, not_4_out, not_7_out, not_9_out);
  or or_94 (or_94_out, X1, not_4_out, not_7_out, not_8_out);
  or or_95 (or_95_out, not_3_out, Y1, not_8_out, not_9_out);
  or or_96 (or_96_out, not_3_out, X0, not_7_out, Y0);
  or or_97 (or_97_out, not_3_out, X0, not_7_out, Ci);
  or or_98 (or_98_out, not_3_out, not_4_out, Y1, not_9_out);
  or or_99 (or_99_out, not_3_out, not_4_out, Y1, not_8_out);
  or or_100 (or_100_out, not_3_out, not_7_out, Y0, Ci);
  or or_101 (or_101_out, X0, Y0, Ci);
  or or_102 (or_102_out, X0, not_8_out, not_9_out);
  or or_103 (or_103_out, not_4_out, Y0, not_9_out);
  or or_104 (or_104_out, not_4_out, not_8_out, Ci);
  or or_105 (or_105_out, X3, Y3);
  or or_106 (or_106_out, X3, X2, Y2);
  or or_107 (or_107_out, X3, X2, X1, Y1);
  or or_108 (or_108_out, X3, X2, X1, X0, Y0);
  or or_109 (or_109_out, X3, X2, X1, X0, Ci);
  or or_110 (or_110_out, X3, X2, X1, Y0, Ci);
  or or_111 (or_111_out, X3, X2, X0, Y1, Y0);
  or or_112 (or_112_out, X3, X2, X0, Y1, Ci);
  or or_113 (or_113_out, X3, X2, Y1, Y0, Ci);
  or or_114 (or_114_out, X3, X1, Y2, Y1);
  or or_115 (or_115_out, X3, X1, X0, Y2, Y0);
  or or_116 (or_116_out, X3, X1, X0, Y2, Ci);
  or or_117 (or_117_out, X3, X1, Y2, Y0, Ci);
  or or_118 (or_118_out, X3, X0, Y2, Y1, Y0);
  or or_119 (or_119_out, X3, X0, Y2, Y1, Ci);
  or or_120 (or_120_out, X3, Y2, Y1, Y0, Ci);
  or or_121 (or_121_out, X2, Y3, Y2);
  or or_122 (or_122_out, X2, X1, Y3, Y1);
  or or_123 (or_123_out, X2, X1, X0, Y3, Y0);
  or or_124 (or_124_out, X2, X1, X0, Y3, Ci);
  or or_125 (or_125_out, X2, X1, Y3, Y0, Ci);
  or or_126 (or_126_out, X2, X0, Y3, Y1, Y0);
  or or_127 (or_127_out, X2, X0, Y3, Y1, Ci);
  or or_128 (or_128_out, X2, Y3, Y1, Y0, Ci);
  or or_129 (or_129_out, X1, Y3, Y2, Y1);
  or or_130 (or_130_out, X1, X0, Y3, Y2, Y0);
  or or_131 (or_131_out, X1, X0, Y3, Y2, Ci);
  or or_132 (or_132_out, X1, Y3, Y2, Y0, Ci);
  or or_133 (or_133_out, X0, Y3, Y2, Y1, Y0);
  or or_134 (or_134_out, X0, Y3, Y2, Y1, Ci);
  or or_135 (or_135_out, Y3, Y2, Y1, Y0, Ci);
  and and_1 (S0, or_101_out, or_102_out, or_103_out, or_104_out);
  and and_2 (S1, or_89_out, or_90_out, or_91_out, or_92_out, or_93_out, or_94_out, or_95_out, or_96_out, or_97_out, or_98_out, or_99_out, or_100_out);
  and and_3 (S2, or_61_out, or_62_out, or_63_out, or_64_out, or_65_out, or_66_out, or_67_out, or_68_out, or_69_out, or_70_out, or_71_out, or_72_out, or_73_out, or_74_out, or_75_out, or_76_out, or_77_out, or_78_out, or_79_out, or_80_out, or_81_out, or_82_out, or_83_out, or_84_out, or_85_out, or_86_out, or_87_out, or_88_out);
  and and_4 (Co, or_105_out, or_106_out, or_107_out, or_108_out, or_109_out, or_110_out, or_111_out, or_112_out, or_113_out, or_114_out, or_115_out, or_116_out, or_117_out, or_118_out, or_119_out, or_120_out, or_121_out, or_122_out, or_123_out, or_124_out, or_125_out, or_126_out, or_127_out, or_128_out, or_129_out, or_130_out, or_131_out, or_132_out, or_133_out, or_134_out, or_135_out);
  and and_5 (S3, or_1_out, or_2_out, or_3_out, or_4_out, or_5_out, or_6_out, or_7_out, or_8_out, or_9_out, or_10_out, or_11_out, or_12_out, or_13_out, or_14_out, or_15_out, or_16_out, or_17_out, or_18_out, or_19_out, or_20_out, or_21_out, or_22_out, or_23_out, or_24_out, or_25_out, or_26_out, or_27_out, or_28_out, or_29_out, or_30_out, or_31_out, or_32_out, or_33_out, or_34_out, or_35_out, or_36_out, or_37_out, or_38_out, or_39_out, or_40_out, or_41_out, or_42_out, or_43_out, or_44_out, or_45_out, or_46_out, or_47_out, or_48_out, or_49_out, or_50_out, or_51_out, or_52_out, or_53_out, or_54_out, or_55_out, or_56_out, or_57_out, or_58_out, or_59_out, or_60_out);
endmodule
